# Fritzing sketch schéma 1 (saved by Fritzing 0.8.7b)

parts:
  MPU-6050 = MPU-6050 Board GY-521 [form="♀ (female)" package=THT]
  Start_/_Finish = Momentary Switch [package=ksa_sealed_tac_switch]
  On_/_Off = Toggle Switch [package=THT]
  LiFEPO4_3_2V_600mAh = Battery Holders [package=battery-aa-kit]
  J4 = single row smd male pin header, 4 pins [form="♂ (male)"]
  J1 = single row smd female pin header, 4 pins [form="♀ (female)"]
  ESP-8266_D1_Mini = WeMos D1 Mini

nets:
  N1: MPU-6050.pin1, J1.pin1
  N2: MPU-6050.pin2, J1.pin2
  N3: MPU-6050.pin3, J1.pin3
  N4: MPU-6050.pin4, J1.pin4
  N5: Start_/_Finish.1, LiFEPO4_3_2V_600mAh.+, J4.pin2, ESP-8266_D1_Mini.G
  N6: Start_/_Finish.3, ESP-8266_D1_Mini.D0
  N7: On_/_Off.L1, ESP-8266_D1_Mini.5V
  N8: On_/_Off.COM, LiFEPO4_3_2V_600mAh.-
  N9: J4.pin1, ESP-8266_D1_Mini.3V3
  N10: J4.pin3, ESP-8266_D1_Mini.D4
  N11: J4.pin4, ESP-8266_D1_Mini.D3

custom parts:
  MPU-6050 Board GY-521: Acelerometro y Giroscopio MPU-6050 Board GY-521
  WeMos D1 Mini: The D1 mini is a mini wifi board based on ESP-8266EX.
