# Fritzing sketch schéma 2 avec sdcard (saved by Fritzing 0.8.7b)
circuit board: 5.80242cm x 4.54189cm

parts:
  ESP-8266_D1_Mini1 = WeMos D1 Mini
  MPU-6051 = MPU-6050 Board GY-521 [form="♀ (female)" package=THT]
  LiFEPO4_3_2V_600mAh1 = Battery Holders [package=battery-aa-kit]
  Start_/_Finish1 = Momentary Switch [package=ksa_sealed_tac_switch]
  On_/_Off1 = Toggle Switch [package=THT]
  J5 = single row smd female pin header, 4 pins [form="♀ (female)"]
  J6 = single row smd male pin header, 4 pins [form="♂ (male)"]
  MicroSD_card_module = Micro SD card reader
  R1 = Resistor [tolerance=±5% resistance=10k package="0603 [SMD]"]

nets:
  N1: ESP-8266_D1_Mini1.3V3, J6.pin1, MicroSD_card_module.Pin_2
  N2: ESP-8266_D1_Mini1.5V, Start_/_Finish1.1, On_/_Off1.L1
  N3: ESP-8266_D1_Mini1.D0, Start_/_Finish1.3, R1.Pin_1
  N4: ESP-8266_D1_Mini1.D3, J6.pin4
  N5: ESP-8266_D1_Mini1.D4, J6.pin3
  N6: ESP-8266_D1_Mini1.D5, MicroSD_card_module.Pin_6
  N7: ESP-8266_D1_Mini1.D6, MicroSD_card_module.Pin_5
  N8: ESP-8266_D1_Mini1.D7, MicroSD_card_module.Pin_4
  N9: ESP-8266_D1_Mini1.D8, MicroSD_card_module.Pin_3
  N10: ESP-8266_D1_Mini1.G, R1.Pin_0
  N11: MPU-6051.pin1, J5.pin1
  N12: MPU-6051.pin2, J5.pin2
  N13: MPU-6051.pin3, J5.pin3
  N14: MPU-6051.pin4, J5.pin4
  N15: LiFEPO4_3_2V_600mAh1.+, J6.pin2, MicroSD_card_module.Pin_1
  N16: LiFEPO4_3_2V_600mAh1.-, On_/_Off1.COM

custom parts:
  WeMos D1 Mini: The D1 mini is a mini wifi board based on ESP-8266EX.
  MPU-6050 Board GY-521: Acelerometro y Giroscopio MPU-6050 Board GY-521
  Micro SD card reader: Micro SD card reader.
